# Fritzing sketch bg (saved by Fritzing 0.9.3b)
circuit board: 19.2cm x 10.8cm
breadboards: 1

parts:
  Součástka1 = JeePlug experimenter's board
  Součástka2 = JeePlug experimenter's board

nets:
  N1: Součástka1.B1, Součástka2.B6
  N2: Součástka1.A4, Součástka1.A5
  N3: Součástka2.B4, Součástka2.B5
  N4: Součástka2.A3, Součástka2.A4, Součástka2.A5
